// Logisim project alu.circ as structural Verilog: 14 circuits, main circuit main
module main (
  input  [15:0] X,
  input  [15:0] Y,
  input  [2:0] switch__S,
  output signed_overflow,
  output [15:0] result,
  output equal
);

  wire [15:0] adder_subtracter_1_result, bitwise_and_1_out_3, bitwise_or_1_out_3,
       logical_left_shifter_1_out_3, right_shifter_1_out_4, set_less_than_1_result;

  Bitwise_OR bitwise_or_1 (.A(X), .B(Y), .out_3(bitwise_or_1_out_3));
  Bitwise_AND bitwise_and_1 (.A(X), .B(Y), .out_3(bitwise_and_1_out_3));
  Adder_Subtracter adder_subtracter_1 (
    .A(X), .B(Y), .Signed_Overflow(signed_overflow), .Add_Subtract(switch__S[0]),
    .Result(adder_subtracter_1_result));  // open: Unsigned_Overflow
  Logical_Left_Shifter logical_left_shifter_1 (.A(X), .B__shamt(Y[3:0]), .out_3(logical_left_shifter_1_out_3));
  Right_Shifter right_shifter_1 (
    .A(X), .B__shamt(Y[3:0]), .Zero_extend_sign_extend(switch__S[1]), .out_4(right_shifter_1_out_4));
  Set_Less_Than set_less_than_1 (.A(X), .B(Y), .Result(set_less_than_1_result));
  Equality equality_1 (.A(X), .B(Y), .out_3(equal));
  Multiplexer #(.select(3), .width(16)) multiplexer_1 (
    .in0(bitwise_or_1_out_3), .in1(bitwise_and_1_out_3), .in2(adder_subtracter_1_result),
    .in3(adder_subtracter_1_result), .in4(logical_left_shifter_1_out_3), .in5(right_shifter_1_out_4),
    .in6(right_shifter_1_out_4), .in7(set_less_than_1_result), .out(result), .sel(switch__S));  // open: en

  // Other names for the same wires on the sheet: ALU_select[2:0] = switch__S
endmodule

module Bitwise_OR (
  input  [15:0] A,
  input  [15:0] B,
  output [15:0] out_3
);

  assign out_3 = A | B;  // OR_Gate or_1, 16 bits wide
endmodule

module Bitwise_AND (
  input  [15:0] A,
  input  [15:0] B,
  output [15:0] out_3
);

  assign out_3 = A & B;  // AND_Gate and_1, 16 bits wide
endmodule

module _1_bit_Adder (
  input  in_1,
  input  in_2,
  input  in_3,
  output out_4,
  output out_5
);

  wire and_1_out, and_2_out, and_3_out;

  and and_1 (and_1_out, in_1, in_2);
  and and_2 (and_2_out, in_2, in_3);
  and and_3 (and_3_out, in_1, in_3);
  or or_1 (out_4, and_1_out, and_2_out, and_3_out);
  xor xor_1 (out_5, in_2, in_1, in_3);
endmodule

module _4_bit_Adder_Block (
  input  [3:0] in_1,
  input  [3:0] in_2,
  input  in_3,
  output out_4,
  output [3:0] out_5
);

  wire n1_bit_adder_2_out_4, n1_bit_adder_3_out_4, n1_bit_adder_4_out_4;

  _1_bit_Adder u_1_bit_adder_1 (
    .in_1(in_1[3]), .in_2(in_2[3]), .out_4(out_4), .in_3(n1_bit_adder_2_out_4), .out_5(out_5[3]));
  _1_bit_Adder u_1_bit_adder_2 (
    .in_1(in_1[2]), .in_2(in_2[2]), .out_4(n1_bit_adder_2_out_4), .in_3(n1_bit_adder_3_out_4),
    .out_5(out_5[2]));
  _1_bit_Adder u_1_bit_adder_3 (
    .in_1(in_1[1]), .in_2(in_2[1]), .out_4(n1_bit_adder_3_out_4), .in_3(n1_bit_adder_4_out_4),
    .out_5(out_5[1]));
  _1_bit_Adder u_1_bit_adder_4 (
    .in_1(in_1[0]), .in_2(in_2[0]), .out_4(n1_bit_adder_4_out_4), .in_3(in_3), .out_5(out_5[0]));
endmodule

module Inverter (
  input  [15:0] A,
  output [15:0] Not_A
);

  wire [15:0] not_1_out;

  not not_1 (not_1_out[0], A[0]);
  not not_2 (not_1_out[1], A[1]);
  not not_3 (not_1_out[2], A[2]);
  not not_4 (not_1_out[3], A[3]);
  not not_5 (not_1_out[4], A[4]);
  not not_6 (not_1_out[5], A[5]);
  not not_7 (not_1_out[6], A[6]);
  not not_8 (not_1_out[7], A[7]);
  not not_9 (not_1_out[8], A[8]);
  not not_10 (not_1_out[9], A[9]);
  not not_11 (not_1_out[10], A[10]);
  not not_12 (not_1_out[11], A[11]);
  not not_13 (not_1_out[12], A[12]);
  not not_14 (not_1_out[13], A[13]);
  not not_15 (not_1_out[14], A[14]);
  not not_16 (not_1_out[15], A[15]);
  Adder #(.width(16)) adder_1 (.a(not_1_out), .b(16'h1), .out(Not_A));  // open: cin, cout
endmodule

module Adder_Subtracter (
  input  [15:0] A,
  input  [15:0] B,
  input  Add_Subtract,
  output Signed_Overflow,
  output Unsigned_Overflow,
  output [15:0] Result
);

  wire and_1_out, n4_bit_adder_block_2_out_4, n4_bit_adder_block_3_out_4, n4_bit_adder_block_4_out_4;
  wire [15:0] inverter_1_not_a, inverter_2_not_a, inverter_3_not_a, multiplexer_1_out, multiplexer_2_out,
       multiplexer_3_out;

  Inverter inverter_1 (.A(A), .Not_A(inverter_1_not_a));
  Inverter inverter_2 (.A(B), .Not_A(inverter_2_not_a));
  Multiplexer #(.width(16)) multiplexer_1 (
    .in0(A), .in1(inverter_1_not_a), .out(multiplexer_1_out), .sel(A[15]));  // open: en
  Multiplexer #(.width(16)) multiplexer_2 (
    .in0(B), .in1(inverter_2_not_a), .out(multiplexer_2_out), .sel(B[15]));  // open: en
  Multiplexer #(.width(16)) multiplexer_3 (
    .in0(multiplexer_2_out), .in1(inverter_3_not_a), .out(multiplexer_3_out), .sel(Add_Subtract));  // open: en
  Inverter inverter_3 (.A(multiplexer_2_out), .Not_A(inverter_3_not_a));
  _4_bit_Adder_Block u_4_bit_adder_block_1 (
    .in_1(multiplexer_1_out[15:12]), .in_2(multiplexer_3_out[15:12]), .out_4(Unsigned_Overflow),
    .in_3(n4_bit_adder_block_2_out_4), .out_5(Result[15:12]));
  _4_bit_Adder_Block u_4_bit_adder_block_2 (
    .in_1(multiplexer_1_out[11:8]), .in_2(multiplexer_3_out[11:8]), .out_4(n4_bit_adder_block_2_out_4),
    .in_3(n4_bit_adder_block_3_out_4), .out_5(Result[11:8]));
  _4_bit_Adder_Block u_4_bit_adder_block_3 (
    .in_1(multiplexer_1_out[7:4]), .in_2(multiplexer_3_out[7:4]), .out_4(n4_bit_adder_block_3_out_4),
    .in_3(n4_bit_adder_block_4_out_4), .out_5(Result[7:4]));
  _4_bit_Adder_Block u_4_bit_adder_block_4 (
    .in_1(multiplexer_1_out[3:0]), .in_2(multiplexer_3_out[3:0]), .out_4(n4_bit_adder_block_4_out_4),
    .in_3(1'b0), .out_5(Result[3:0]));
  and and_1 (and_1_out, A[15], B[15]);
  xor xor_1 (Signed_Overflow, and_1_out, Result[15]);

  // Other names for the same wires on the sheet: A_negative = A[15]; B_negative = B[15]

  // Notes on the sheet:
  //   Add_Subtract: pull=up
endmodule

module Logical_Left_Shifter (
  input  [15:0] A,
  input  [3:0] B__shamt,
  output [15:0] out_3
);

  Multiplexer #(.select(4), .width(16)) multiplexer_1 (
    .in0(A), .in1({A[14:0], 1'b0}), .in2({A[13:0], 2'b00}), .in3({A[12:0], 3'b000}),
    .in4({A[11:0], 4'b0000}), .in5({A[10:0], {5{1'b0}}}), .in6({A[9:0], {6{1'b0}}}),
    .in7({A[8:0], {7{1'b0}}}), .in8({A[7:0], {8{1'b0}}}), .in9({A[6:0], {9{1'b0}}}),
    .in10({A[5:0], {10{1'b0}}}), .in11({A[4:0], {11{1'b0}}}), .in12({A[3:0], {12{1'b0}}}),
    .in13({A[2:0], {13{1'b0}}}), .in14({A[1:0], {14{1'b0}}}), .in15({A[0], {15{1'b0}}}), .out(out_3),
    .sel(B__shamt));  // open: en
endmodule

module Right_Shifter (
  input  [15:0] A,
  input  [3:0] B__shamt,
  input  Zero_extend_sign_extend,
  output [15:0] out_4
);

  wire [15:0] bit_extender_1_out, bit_extender_2_out, bit_extender_3_out, bit_extender_4_out,
       bit_extender_5_out, bit_extender_6_out, bit_extender_7_out, bit_extender_8_out, bit_extender_9_out,
       bit_extender_10_out, bit_extender_11_out, bit_extender_12_out, bit_extender_13_out,
       bit_extender_14_out, bit_extender_15_out, bit_extender_16_out, bit_extender_17_out,
       bit_extender_18_out, bit_extender_19_out, bit_extender_20_out, bit_extender_21_out,
       bit_extender_22_out, bit_extender_23_out, bit_extender_24_out, bit_extender_25_out,
       bit_extender_26_out, bit_extender_27_out, bit_extender_28_out, bit_extender_29_out,
       bit_extender_30_out, multiplexer_1_out, multiplexer_2_out, multiplexer_3_out, multiplexer_4_out,
       multiplexer_5_out, multiplexer_6_out, multiplexer_7_out, multiplexer_8_out, multiplexer_9_out,
       multiplexer_10_out, multiplexer_11_out, multiplexer_12_out, multiplexer_13_out, multiplexer_14_out,
       multiplexer_15_out;

  assign bit_extender_1_out = {{1{1'b0}}, A[15:1]};  // Bit_Extender bit_extender_1
  assign bit_extender_2_out = {{1{A[15]}}, A[15:1]};  // Bit_Extender bit_extender_2
  assign bit_extender_3_out = {{2{1'b0}}, A[15:2]};  // Bit_Extender bit_extender_3
  assign bit_extender_4_out = {{2{A[15]}}, A[15:2]};  // Bit_Extender bit_extender_4
  assign bit_extender_5_out = {{3{1'b0}}, A[15:3]};  // Bit_Extender bit_extender_5
  assign bit_extender_6_out = {{3{A[15]}}, A[15:3]};  // Bit_Extender bit_extender_6
  assign bit_extender_7_out = {{4{1'b0}}, A[15:4]};  // Bit_Extender bit_extender_7
  assign bit_extender_8_out = {{4{A[15]}}, A[15:4]};  // Bit_Extender bit_extender_8
  assign bit_extender_9_out = {{5{1'b0}}, A[15:5]};  // Bit_Extender bit_extender_9
  assign bit_extender_10_out = {{5{A[15]}}, A[15:5]};  // Bit_Extender bit_extender_10
  assign bit_extender_11_out = {{6{1'b0}}, A[15:6]};  // Bit_Extender bit_extender_11
  assign bit_extender_12_out = {{6{A[15]}}, A[15:6]};  // Bit_Extender bit_extender_12
  assign bit_extender_13_out = {{7{1'b0}}, A[15:7]};  // Bit_Extender bit_extender_13
  assign bit_extender_14_out = {{7{A[15]}}, A[15:7]};  // Bit_Extender bit_extender_14
  assign bit_extender_15_out = {{8{1'b0}}, A[15:8]};  // Bit_Extender bit_extender_15
  assign bit_extender_16_out = {{8{A[15]}}, A[15:8]};  // Bit_Extender bit_extender_16
  assign bit_extender_17_out = {{9{1'b0}}, A[15:9]};  // Bit_Extender bit_extender_17
  assign bit_extender_18_out = {{9{A[15]}}, A[15:9]};  // Bit_Extender bit_extender_18
  assign bit_extender_19_out = {{10{1'b0}}, A[15:10]};  // Bit_Extender bit_extender_19
  assign bit_extender_20_out = {{10{A[15]}}, A[15:10]};  // Bit_Extender bit_extender_20
  assign bit_extender_21_out = {{11{1'b0}}, A[15:11]};  // Bit_Extender bit_extender_21
  assign bit_extender_22_out = {{11{A[15]}}, A[15:11]};  // Bit_Extender bit_extender_22
  assign bit_extender_23_out = {{12{1'b0}}, A[15:12]};  // Bit_Extender bit_extender_23
  assign bit_extender_24_out = {{12{A[15]}}, A[15:12]};  // Bit_Extender bit_extender_24
  assign bit_extender_25_out = {{13{1'b0}}, A[15:13]};  // Bit_Extender bit_extender_25
  assign bit_extender_26_out = {{13{A[15]}}, A[15:13]};  // Bit_Extender bit_extender_26
  assign bit_extender_27_out = {{14{1'b0}}, A[15:14]};  // Bit_Extender bit_extender_27
  assign bit_extender_28_out = {{14{A[15]}}, A[15:14]};  // Bit_Extender bit_extender_28
  assign bit_extender_29_out = {{15{1'b0}}, A[15]};  // Bit_Extender bit_extender_29
  assign bit_extender_30_out = {{15{A[15]}}, A[15]};  // Bit_Extender bit_extender_30
  Multiplexer #(.width(16)) multiplexer_1 (
    .in0(bit_extender_1_out), .in1(bit_extender_2_out), .out(multiplexer_1_out), .sel(Zero_extend_sign_extend));  // open: en
  Multiplexer #(.width(16)) multiplexer_2 (
    .in0(bit_extender_3_out), .in1(bit_extender_4_out), .out(multiplexer_2_out), .sel(Zero_extend_sign_extend));  // open: en
  Multiplexer #(.width(16)) multiplexer_3 (
    .in0(bit_extender_5_out), .in1(bit_extender_6_out), .out(multiplexer_3_out), .sel(Zero_extend_sign_extend));  // open: en
  Multiplexer #(.width(16)) multiplexer_4 (
    .in0(bit_extender_7_out), .in1(bit_extender_8_out), .out(multiplexer_4_out), .sel(Zero_extend_sign_extend));  // open: en
  Multiplexer #(.width(16)) multiplexer_5 (
    .in0(bit_extender_9_out), .in1(bit_extender_10_out), .out(multiplexer_5_out),
    .sel(Zero_extend_sign_extend));  // open: en
  Multiplexer #(.width(16)) multiplexer_6 (
    .in0(bit_extender_11_out), .in1(bit_extender_12_out), .out(multiplexer_6_out),
    .sel(Zero_extend_sign_extend));  // open: en
  Multiplexer #(.width(16)) multiplexer_7 (
    .in0(bit_extender_13_out), .in1(bit_extender_14_out), .out(multiplexer_7_out),
    .sel(Zero_extend_sign_extend));  // open: en
  Multiplexer #(.width(16)) multiplexer_8 (
    .in0(bit_extender_15_out), .in1(bit_extender_16_out), .out(multiplexer_8_out),
    .sel(Zero_extend_sign_extend));  // open: en
  Multiplexer #(.width(16)) multiplexer_9 (
    .in0(bit_extender_17_out), .in1(bit_extender_18_out), .out(multiplexer_9_out),
    .sel(Zero_extend_sign_extend));  // open: en
  Multiplexer #(.width(16)) multiplexer_10 (
    .in0(bit_extender_19_out), .in1(bit_extender_20_out), .out(multiplexer_10_out),
    .sel(Zero_extend_sign_extend));  // open: en
  Multiplexer #(.width(16)) multiplexer_11 (
    .in0(bit_extender_21_out), .in1(bit_extender_22_out), .out(multiplexer_11_out),
    .sel(Zero_extend_sign_extend));  // open: en
  Multiplexer #(.width(16)) multiplexer_12 (
    .in0(bit_extender_23_out), .in1(bit_extender_24_out), .out(multiplexer_12_out),
    .sel(Zero_extend_sign_extend));  // open: en
  Multiplexer #(.width(16)) multiplexer_13 (
    .in0(bit_extender_25_out), .in1(bit_extender_26_out), .out(multiplexer_13_out),
    .sel(Zero_extend_sign_extend));  // open: en
  Multiplexer #(.width(16)) multiplexer_14 (
    .in0(bit_extender_27_out), .in1(bit_extender_28_out), .out(multiplexer_14_out),
    .sel(Zero_extend_sign_extend));  // open: en
  Multiplexer #(.width(16)) multiplexer_15 (
    .in0(bit_extender_29_out), .in1(bit_extender_30_out), .out(multiplexer_15_out),
    .sel(Zero_extend_sign_extend));  // open: en
  Multiplexer #(.select(4), .width(16)) multiplexer_16 (
    .in0(A), .in1(multiplexer_1_out), .in2(multiplexer_2_out), .in3(multiplexer_3_out),
    .in4(multiplexer_4_out), .in5(multiplexer_5_out), .in6(multiplexer_6_out), .in7(multiplexer_7_out),
    .in8(multiplexer_8_out), .in9(multiplexer_9_out), .in10(multiplexer_10_out), .in11(multiplexer_11_out),
    .in12(multiplexer_12_out), .in13(multiplexer_13_out), .in14(multiplexer_14_out),
    .in15(multiplexer_15_out), .out(out_4), .sel(B__shamt));  // open: en

  // Other names for the same wires on the sheet: shamt[3:0] = B__shamt
endmodule

module Set_Less_Than (
  input  [15:0] A,
  input  [15:0] B,
  output [15:0] Result
);

  wire A6, n1_bit_less_than_1_out_4, n1_bit_less_than_2_out_4, n1_bit_less_than_3_out_4,
       n1_bit_less_than_4_out_4, n1_bit_less_than_5_out_4, n1_bit_less_than_6_out_4,
       n1_bit_less_than_7_out_4, n1_bit_less_than_8_out_4, n1_bit_less_than_9_out_4,
       n1_bit_less_than_10_out_4, n1_bit_less_than_11_out_4, n1_bit_less_than_12_out_4,
       n1_bit_less_than_13_out_4, n1_bit_less_than_14_out_4, n1_bit_less_than_15_out_4,
       n1_bit_less_than_16_out_4;
  wire [15:0] inverter_1_not_a, inverter_2_not_a, multiplexer_1_out, multiplexer_2_out;

  Inverter inverter_1 (.A(A), .Not_A(inverter_1_not_a));
  Inverter inverter_2 (.A(B), .Not_A(inverter_2_not_a));
  Multiplexer #(.width(16)) multiplexer_1 (
    .in0(A), .in1(inverter_1_not_a), .out({multiplexer_1_out[15:7], A6, multiplexer_1_out[5:0]}), .sel(A[15]));  // open: en
  Multiplexer #(.width(16)) multiplexer_2 (
    .in0(B), .in1(inverter_2_not_a), .out(multiplexer_2_out), .sel(B[15]));  // open: en
  _1_bit_Less_Than u_1_bit_less_than_1 (
    .A(multiplexer_1_out[15]), .B(multiplexer_2_out[15]), .in_1(1'b0), .out_4(n1_bit_less_than_1_out_4));
  _1_bit_Less_Than u_1_bit_less_than_2 (
    .A(multiplexer_1_out[14]), .B(multiplexer_2_out[14]), .in_1(n1_bit_less_than_1_out_4),
    .out_4(n1_bit_less_than_2_out_4));
  _1_bit_Less_Than u_1_bit_less_than_3 (
    .A(multiplexer_1_out[13]), .B(multiplexer_2_out[13]), .in_1(n1_bit_less_than_2_out_4),
    .out_4(n1_bit_less_than_3_out_4));
  _1_bit_Less_Than u_1_bit_less_than_4 (
    .A(multiplexer_1_out[12]), .B(multiplexer_2_out[12]), .in_1(n1_bit_less_than_3_out_4),
    .out_4(n1_bit_less_than_4_out_4));
  _1_bit_Less_Than u_1_bit_less_than_5 (
    .A(multiplexer_1_out[11]), .B(multiplexer_2_out[11]), .in_1(n1_bit_less_than_4_out_4),
    .out_4(n1_bit_less_than_5_out_4));
  _1_bit_Less_Than u_1_bit_less_than_6 (
    .A(multiplexer_1_out[10]), .B(multiplexer_2_out[10]), .in_1(n1_bit_less_than_5_out_4),
    .out_4(n1_bit_less_than_6_out_4));
  _1_bit_Less_Than u_1_bit_less_than_7 (
    .A(multiplexer_1_out[9]), .B(multiplexer_2_out[9]), .in_1(n1_bit_less_than_6_out_4),
    .out_4(n1_bit_less_than_7_out_4));
  _1_bit_Less_Than u_1_bit_less_than_8 (
    .A(multiplexer_1_out[8]), .B(multiplexer_2_out[8]), .in_1(n1_bit_less_than_7_out_4),
    .out_4(n1_bit_less_than_8_out_4));
  _1_bit_Less_Than u_1_bit_less_than_9 (
    .A(multiplexer_1_out[7]), .B(multiplexer_2_out[7]), .in_1(n1_bit_less_than_8_out_4),
    .out_4(n1_bit_less_than_9_out_4));
  _1_bit_Less_Than u_1_bit_less_than_10 (
    .A(A6), .B(multiplexer_2_out[6]), .in_1(n1_bit_less_than_9_out_4), .out_4(n1_bit_less_than_10_out_4));
  _1_bit_Less_Than u_1_bit_less_than_11 (
    .A(multiplexer_1_out[5]), .B(multiplexer_2_out[5]), .in_1(n1_bit_less_than_10_out_4),
    .out_4(n1_bit_less_than_11_out_4));
  _1_bit_Less_Than u_1_bit_less_than_12 (
    .A(multiplexer_1_out[4]), .B(multiplexer_2_out[4]), .in_1(n1_bit_less_than_11_out_4),
    .out_4(n1_bit_less_than_12_out_4));
  _1_bit_Less_Than u_1_bit_less_than_13 (
    .A(multiplexer_1_out[3]), .B(multiplexer_2_out[3]), .in_1(n1_bit_less_than_12_out_4),
    .out_4(n1_bit_less_than_13_out_4));
  _1_bit_Less_Than u_1_bit_less_than_14 (
    .A(multiplexer_1_out[2]), .B(multiplexer_2_out[2]), .in_1(n1_bit_less_than_13_out_4),
    .out_4(n1_bit_less_than_14_out_4));
  _1_bit_Less_Than u_1_bit_less_than_15 (
    .A(multiplexer_1_out[1]), .B(multiplexer_2_out[1]), .in_1(n1_bit_less_than_14_out_4),
    .out_4(n1_bit_less_than_15_out_4));
  _1_bit_Less_Than u_1_bit_less_than_16 (
    .A(multiplexer_1_out[0]), .B(multiplexer_2_out[0]), .in_1(n1_bit_less_than_15_out_4),
    .out_4(n1_bit_less_than_16_out_4));
  assign Result = {{15{1'b0}}, n1_bit_less_than_16_out_4};  // Bit_Extender bit_extender_1
endmodule

module _1_bit_Less_Than (
  input  in_1,
  input  A,
  input  B,
  output out_4
);

  wire and_1_out, not_1_out;

  not not_1 (not_1_out, A);
  and and_1 (and_1_out, not_1_out, B);
  or or_1 (out_4, and_1_out, in_1);
endmodule

module _1_bit_Equality (
  input  in_1,
  input  in_2,
  input  in_3,
  output out_4
);

  wire and_1_out, and_2_out, not_1_out, not_2_out, or_1_out;

  not not_1 (not_1_out, in_2);
  not not_2 (not_2_out, in_3);
  and and_1 (and_1_out, in_3, in_2);
  and and_2 (and_2_out, not_1_out, not_2_out);
  and and_3 (out_4, in_1, or_1_out);
  or or_1 (or_1_out, and_1_out, and_2_out);
endmodule

module Equality (
  input  [15:0] A,
  input  [15:0] B,
  output out_3
);

  wire n4_bit_equality_1_equal, n4_bit_equality_2_equal, n4_bit_equality_3_equal;

  _4_bit_Equality u_4_bit_equality_1 (.A(A[3:0]), .B(B[3:0]), .Carry_over(1'b1), .Equal(n4_bit_equality_1_equal));
  _4_bit_Equality u_4_bit_equality_2 (
    .A(A[7:4]), .B(B[7:4]), .Carry_over(n4_bit_equality_1_equal), .Equal(n4_bit_equality_2_equal));
  _4_bit_Equality u_4_bit_equality_3 (
    .A(A[11:8]), .B(B[11:8]), .Carry_over(n4_bit_equality_2_equal), .Equal(n4_bit_equality_3_equal));
  _4_bit_Equality u_4_bit_equality_4 (.A(A[15:12]), .B(B[15:12]), .Carry_over(n4_bit_equality_3_equal), .Equal(out_3));
endmodule

module _4_bit_Equality (
  input  Carry_over,
  input  [3:0] A,
  input  [3:0] B,
  output Equal
);

  wire n1_bit_equality_1_out_4, n1_bit_equality_2_out_4, n1_bit_equality_3_out_4;

  _1_bit_Equality u_1_bit_equality_1 (.in_2(A[0]), .in_3(B[0]), .in_1(Carry_over), .out_4(n1_bit_equality_1_out_4));
  _1_bit_Equality u_1_bit_equality_2 (
    .in_2(A[1]), .in_3(B[1]), .in_1(n1_bit_equality_1_out_4), .out_4(n1_bit_equality_2_out_4));
  _1_bit_Equality u_1_bit_equality_3 (
    .in_2(A[2]), .in_3(B[2]), .in_1(n1_bit_equality_2_out_4), .out_4(n1_bit_equality_3_out_4));
  _1_bit_Equality u_1_bit_equality_4 (.in_2(A[3]), .in_3(B[3]), .in_1(n1_bit_equality_3_out_4), .out_4(Equal));
endmodule
