// Logisim project alu-harness.circ as structural Verilog: 1 circuit, main circuit main
module main (
  output [7:0] Test_num,
  output Signed_Overflow,
  output [15:0] Result,
  output Equal
);

  wire clock_1_out;
  wire [2:0] rom_2_data;
  wire [7:0] adder_1_out;
  wire [31:0] rom_1_data;

  Register register_1 (.D(adder_1_out), .Q(Test_num), .clk(clock_1_out));  // open: en, clr
  Adder adder_1 (.a(8'h1), .b(Test_num), .out(adder_1_out));  // open: cin, cout
  ROM #(.dataWidth(32)) rom_1 (.addr(Test_num), .data(rom_1_data));  // open: sel
  ROM #(.dataWidth(3)) rom_2 (.addr(Test_num), .data(rom_2_data));  // open: sel
  Clock clock_1 (.out(clock_1_out));
  // alu_main main_1: pin names not known; wires that end beside it: rom_1_data[15:0], rom_1_data[31:16], rom_2_data, Signed_Overflow, Result, Equal
endmodule
