// Logisim project cpu.circ as structural Verilog: 2 circuits, main circuit main
module main (
  input  [15:0] From_Instr_Mem,
  input  in_2,
  input  clk,
  output [15:0] r0,
  output [15:0] r1,
  output [15:0] r2,
  output [15:0] r3,
  output [15:0] Display_0,
  output [15:0] Display_1,
  output [15:0] To_Instr_Mem,
  output [15:0] Data_Mem_Data,
  output [15:0] Data_Mem_Addr,
  output Data_Mem_Write
);

  wire addi, and_1_out, and_2_out, and_3_out, and_5_out, and_6_out, andi, beq, beq_bne, blockbottom_1_out_5,
       blockbottom_1_out_6, blockbottom_1_out_7, blockbottom_1_out_8, blockbottom_1_out_9,
       blockbottom_1_out_10, blockbottom_1_out_11, blockbottom_1_out_12, blockbottom_1_out_13,
       blockbottom_1_out_14, blockbottom_1_out_15, blockbottom_1_out_16, blockbottom_1_out_17,
       blockbottom_1_out_18, blockbottom_1_out_19, blockbottom_1_out_20, blockbottom_2_out_5,
       blockbottom_2_out_6, blockbottom_2_out_7, blockbottom_2_out_8, blockbottom_2_out_9,
       blockbottom_2_out_10, blockbottom_2_out_11, blockbottom_2_out_12, blockbottom_2_out_13,
       blockbottom_2_out_14, blockbottom_2_out_15, blockbottom_2_out_16, blockbottom_2_out_17,
       blockbottom_2_out_18, blockbottom_2_out_19, blockbottom_2_out_20, blocktop_1_out_5, blocktop_1_out_6,
       blocktop_1_out_7, blocktop_1_out_8, blocktop_1_out_9, blocktop_1_out_10, blocktop_1_out_11,
       blocktop_1_out_12, blocktop_1_out_13, blocktop_1_out_14, blocktop_1_out_15, blocktop_1_out_16,
       blocktop_1_out_17, blocktop_1_out_18, blocktop_1_out_19, blocktop_1_out_20, blocktop_2_out_5,
       blocktop_2_out_6, blocktop_2_out_7, blocktop_2_out_8, blocktop_2_out_9, blocktop_2_out_10,
       blocktop_2_out_11, blocktop_2_out_12, blocktop_2_out_13, blocktop_2_out_14, blocktop_2_out_15,
       blocktop_2_out_16, blocktop_2_out_17, blocktop_2_out_18, blocktop_2_out_19, blocktop_2_out_20, bne,
       comparator_1_gt, comparator_2_lt, comparator_3_gt, comparator_4_gt, comparator_5_lt, comparator_6_eq,
       comparator_7_eq, disp, i_type, j, j_type, jal, jr, lui, lw, main_2_signed_overflow, mem_reg,
       nand_1_out, not_1_out, not_3_out, not_4_out, not_5_out, or_1_out, ori, r_type, register_2_q,
       register_4_q, RegWrite, tunnel, unsigned_signed;
  wire [1:0] multiplexer_3_out, multiplexer_5_out;
  wire [2:0] alu_switch, funct, multiplexer_4_out;
  wire [3:0] opcode;
  wire [11:3] target_addr;
  wire [15:0] adder_1_out, adder_2_out, and_7_out, bit_extender_1_out, bit_extender_2_out,
       bit_extender_3_out, bit_extender_4_out, Data_In, imm, imm____8, jump_addr, multiplexer_1_out,
       multiplexer_2_out, multiplexer_8_out, multiplexer_9_out, multiplexer_10_out, multiplexer_11_out,
       multiplexer_13_out, or_6_out, rs, subtractor_1_out, Write_Data;

  Register #(.width(16)) register_1 (.D(multiplexer_1_out), .Q(To_Instr_Mem), .clk(clk));  // open: en, clr
  Multiplexer #(.width(16)) multiplexer_1 (
    .in0(multiplexer_2_out), .in1(adder_2_out), .out(multiplexer_1_out), .sel(beq_bne));  // open: en
  or or_1 (or_1_out, beq_bne, j_type);
  Multiplexer #(.width(16)) multiplexer_2 (
    .in0(adder_1_out), .in1(jump_addr), .out(multiplexer_2_out), .sel(j_type));  // open: en
  Adder #(.width(16)) adder_1 (.a(16'h1), .b(To_Instr_Mem), .out(adder_1_out));  // open: cin, cout
  Register #(.width(1)) register_2 (.D(or_1_out), .Q(register_2_q), .clk(clk), .clr(register_4_q));  // open: en
  Clock clock_1 ();  // open: out
  Register #(.width(16)) register_3 (
    .D(From_Instr_Mem), .Q({opcode, target_addr, funct}), .clk(clk), .clr(register_2_q));  // open: en
  Register #(.width(1), .trigger("falling")) register_4 (
    .D(register_2_q), .Q(register_4_q), .clk(clk));  // open: en, clr
  assign bit_extender_1_out = {{8{target_addr[7]}}, {target_addr[7:3], funct}};  // Bit_Extender bit_extender_1
  Multiplexer #(.width(2)) multiplexer_3 (
    .in0(target_addr[9:8]), .in1(target_addr[7:6]), .out(multiplexer_3_out), .sel(r_type));  // open: en
  Multiplexer #(.select(3), .width(3)) multiplexer_4 (
    .in3(3'b000), .in4(3'b010), .in5(3'b001), .out(multiplexer_4_out), .sel(opcode[2:0]));  // open: in0, in1, in2, in6, in7, en
  Adder #(.width(16)) adder_2 (.a(To_Instr_Mem), .b(bit_extender_1_out), .out(adder_2_out));  // open: cin, cout
  assign bit_extender_2_out = {{8{1'b0}}, {target_addr[7:3], funct}};  // Bit_Extender bit_extender_2
  assign bit_extender_3_out = {{8{target_addr[7]}}, {target_addr[7:3], funct}};  // Bit_Extender bit_extender_3
  opcode opcode_1 (
    .opcode(opcode), .out_2(r_type), .out_3(disp), .out_4(lui), .out_5(ori), .out_6(addi), .out_7(andi),
    .out_8(jal), .out_9(j), .out_10(jr), .out_11(beq), .out_12(bne), .out_13(lw), .out_14(Data_Mem_Write));
  not not_1 (not_1_out, tunnel);
  not not_2 (mem_reg, lw);
  Comparator #(.width(4), .mode("unsigned")) comparator_1 (
    .a(opcode), .b(4'b0001), .gt(comparator_1_gt));  // open: eq, lt
  Comparator #(.width(4), .mode("unsigned")) comparator_2 (
    .a(opcode), .b(4'b0110), .lt(comparator_2_lt));  // open: gt, eq
  Multiplexer #(.width(2)) multiplexer_5 (
    .in0(multiplexer_3_out), .in1(2'b11), .out(multiplexer_5_out), .sel(jal));  // open: en
  Multiplexer #(.width(16)) multiplexer_6 (
    .in0(bit_extender_2_out), .in1(bit_extender_3_out), .out(imm), .sel(unsigned_signed));  // open: en
  and and_1 (and_1_out, tunnel, beq);
  or or_2 (beq_bne, and_1_out, and_2_out);
  and and_2 (and_2_out, bne, not_1_out);
  Multiplexer #(.width(3)) multiplexer_7 (
    .in0(funct), .in1(multiplexer_4_out), .out(alu_switch), .sel(not_3_out));  // open: en
  not not_3 (not_3_out, r_type);
  and and_3 (and_3_out, comparator_1_gt, comparator_2_lt);
  Multiplexer #(.width(16)) multiplexer_8 (
    .in0(Write_Data), .in1(subtractor_1_out), .out(multiplexer_8_out), .sel(jal));  // open: en
  Subtractor #(.width(16)) subtractor_1 (.a(To_Instr_Mem), .b(16'h1), .out(subtractor_1_out));  // open: bin, bout
  or or_3 (RegWrite, lw, and_3_out, r_type, jal);
  Comparator #(.width(4), .mode("unsigned")) comparator_3 (
    .a(opcode), .b(4'b1000), .gt(comparator_3_gt));  // open: eq, lt
  Regfile_main main_1 (
    .Read_register_1(target_addr[11:10]), .Read_register_2(target_addr[9:8]),
    .write_register(multiplexer_5_out), .write_data(multiplexer_8_out), .Reg_0_Value(r0), .Reg_1_Value(r1),
    .Reg_2_Value(r2), .Reg_3_Value(r3), .RegWrite(RegWrite), .clock(clk), .Read_Data_1(rs),
    .Read_Data_2(Data_In));
  Comparator #(.width(4), .mode("unsigned")) comparator_4 (
    .a(opcode), .b(4'b0101), .gt(comparator_4_gt));  // open: eq, lt
  Comparator #(.width(4), .mode("unsigned")) comparator_5 (
    .a(opcode), .b(4'b1011), .lt(comparator_5_lt));  // open: gt, eq
  or or_4 (unsigned_signed, addi, comparator_3_gt);
  not not_4 (not_4_out, r_type);
  or or_5 (j_type, jal, j, jr);
  and and_4 (i_type, not_4_out, nand_1_out);
  nand nand_1 (nand_1_out, comparator_4_gt, comparator_5_lt);
  Comparator #(.width(16), .mode("unsigned")) comparator_6 (
    .a(imm), .b({16{1'b0}}), .eq(comparator_6_eq));  // open: gt, lt
  Multiplexer #(.width(16)) multiplexer_9 (
    .in0(Data_In), .in1(imm), .out(multiplexer_9_out), .sel(i_type));  // open: en
  _7_Segment_Display u_7_segment_display_1 (
    .g(blocktop_1_out_5), .f(blocktop_1_out_13), .a(blocktop_1_out_14), .b(blocktop_1_out_6),
    .e(blockbottom_1_out_13), .d(blockbottom_1_out_5), .c(blockbottom_1_out_6), .dp(blockbottom_1_out_14));
  BlockBottom blockbottom_1 (
    .out_13(blockbottom_1_out_13), .out_5(blockbottom_1_out_5), .out_6(blockbottom_1_out_6),
    .out_14(blockbottom_1_out_14), .out_15(blockbottom_1_out_15), .out_7(blockbottom_1_out_7),
    .out_8(blockbottom_1_out_8), .out_16(blockbottom_1_out_16), .out_17(blockbottom_1_out_17),
    .out_9(blockbottom_1_out_9), .out_10(blockbottom_1_out_10), .out_18(blockbottom_1_out_18),
    .out_19(blockbottom_1_out_19), .out_11(blockbottom_1_out_11), .out_12(blockbottom_1_out_12),
    .out_20(blockbottom_1_out_20), .in_1(Display_0[15:12]), .in_2(Display_0[11:8]), .in_3(Display_0[7:4]),
    .in_4(Display_0[3:0]));
  and and_5 (and_5_out, disp, comparator_6_eq);
  LED signed_overflow (.in(main_2_signed_overflow));
  alu_main main_2 (
    .X(rs), .Y(multiplexer_9_out), .switch__S(alu_switch), .signed_overflow(main_2_signed_overflow),
    .result(Data_Mem_Addr), .equal(tunnel));
  BlockTop blocktop_1 (
    .in_1(Display_0[15:12]), .in_2(Display_0[11:8]), .in_3(Display_0[7:4]), .in_4(Display_0[3:0]),
    .out_5(blocktop_1_out_5), .out_13(blocktop_1_out_13), .out_14(blocktop_1_out_14),
    .out_6(blocktop_1_out_6), .out_7(blocktop_1_out_7), .out_15(blocktop_1_out_15),
    .out_16(blocktop_1_out_16), .out_8(blocktop_1_out_8), .out_9(blocktop_1_out_9),
    .out_17(blocktop_1_out_17), .out_18(blocktop_1_out_18), .out_10(blocktop_1_out_10),
    .out_11(blocktop_1_out_11), .out_19(blocktop_1_out_19), .out_20(blocktop_1_out_20),
    .out_12(blocktop_1_out_12));
  _7_Segment_Display u_7_segment_display_2 (
    .g(blocktop_1_out_9), .f(blocktop_1_out_17), .a(blocktop_1_out_18), .b(blocktop_1_out_10),
    .e(blockbottom_1_out_17), .d(blockbottom_1_out_9), .c(blockbottom_1_out_10), .dp(blockbottom_1_out_18));
  _7_Segment_Display u_7_segment_display_3 (
    .g(blocktop_1_out_7), .f(blocktop_1_out_15), .a(blocktop_1_out_16), .b(blocktop_1_out_8),
    .e(blockbottom_1_out_15), .d(blockbottom_1_out_7), .c(blockbottom_1_out_8), .dp(blockbottom_1_out_16));
  Register #(.width(16)) register_5 (.D(multiplexer_10_out), .Q(Display_0), .clk(clk));  // open: en, clr
  Multiplexer #(.width(16), .enable("false")) multiplexer_10 (
    .in0(Display_0), .in1(rs), .out(multiplexer_10_out), .sel(and_5_out));
  Shifter #(.width(16)) shifter_1 (.in(imm), .\dist (4'b1000), .out(imm____8));
  _7_Segment_Display u_7_segment_display_4 (
    .g(blocktop_1_out_11), .f(blocktop_1_out_19), .a(blocktop_1_out_20), .b(blocktop_1_out_12),
    .e(blockbottom_1_out_19), .d(blockbottom_1_out_11), .c(blockbottom_1_out_12), .dp(blockbottom_1_out_20));
  not not_5 (not_5_out, Data_Mem_Write);
  _7_Segment_Display u_7_segment_display_5 (
    .g(blocktop_2_out_5), .f(blocktop_2_out_13), .a(blocktop_2_out_14), .b(blocktop_2_out_6),
    .e(blockbottom_2_out_13), .d(blockbottom_2_out_5), .c(blockbottom_2_out_6), .dp(blockbottom_2_out_14));
  BlockBottom blockbottom_2 (
    .out_13(blockbottom_2_out_13), .out_5(blockbottom_2_out_5), .out_6(blockbottom_2_out_6),
    .out_14(blockbottom_2_out_14), .out_15(blockbottom_2_out_15), .out_7(blockbottom_2_out_7),
    .out_8(blockbottom_2_out_8), .out_16(blockbottom_2_out_16), .out_17(blockbottom_2_out_17),
    .out_9(blockbottom_2_out_9), .out_10(blockbottom_2_out_10), .out_18(blockbottom_2_out_18),
    .out_19(blockbottom_2_out_19), .out_11(blockbottom_2_out_11), .out_12(blockbottom_2_out_12),
    .out_20(blockbottom_2_out_20), .in_1(Display_1[15:12]), .in_2(Display_1[11:8]), .in_3(Display_1[7:4]),
    .in_4(Display_1[3:0]));
  and and_6 (and_6_out, disp, comparator_7_eq);
  Comparator #(.width(16), .mode("unsigned")) comparator_7 (.a(imm), .b(16'h1), .eq(comparator_7_eq));  // open: gt, lt
  assign Data_Mem_Data = Data_Mem_Write ? Data_In : 16'bz;  // Controlled_Buffer controlled_buffer_1
  RAM #(.addrWidth(16), .dataWidth(16)) ram_1 (
    .addr(Data_Mem_Addr), .data(Data_Mem_Data), .sel(1'b1), .clk(clk), .ld(not_5_out), .clr(in_2));
  assign and_7_out = To_Instr_Mem & 16'hf000;  // AND_Gate and_7, 16 bits wide
  assign bit_extender_4_out = {{4{1'b0}}, {target_addr, funct}};  // Bit_Extender bit_extender_4
  BlockTop blocktop_2 (
    .in_1(Display_1[15:12]), .in_2(Display_1[11:8]), .in_3(Display_1[7:4]), .in_4(Display_1[3:0]),
    .out_5(blocktop_2_out_5), .out_13(blocktop_2_out_13), .out_14(blocktop_2_out_14),
    .out_6(blocktop_2_out_6), .out_7(blocktop_2_out_7), .out_15(blocktop_2_out_15),
    .out_16(blocktop_2_out_16), .out_8(blocktop_2_out_8), .out_9(blocktop_2_out_9),
    .out_17(blocktop_2_out_17), .out_18(blocktop_2_out_18), .out_10(blocktop_2_out_10),
    .out_11(blocktop_2_out_11), .out_19(blocktop_2_out_19), .out_20(blocktop_2_out_20),
    .out_12(blocktop_2_out_12));
  _7_Segment_Display u_7_segment_display_6 (
    .g(blocktop_2_out_9), .f(blocktop_2_out_17), .a(blocktop_2_out_18), .b(blocktop_2_out_10),
    .e(blockbottom_2_out_17), .d(blockbottom_2_out_9), .c(blockbottom_2_out_10), .dp(blockbottom_2_out_18));
  _7_Segment_Display u_7_segment_display_7 (
    .g(blocktop_2_out_7), .f(blocktop_2_out_15), .a(blocktop_2_out_16), .b(blocktop_2_out_8),
    .e(blockbottom_2_out_15), .d(blockbottom_2_out_7), .c(blockbottom_2_out_8), .dp(blockbottom_2_out_16));
  Register #(.width(16)) register_6 (.D(multiplexer_11_out), .Q(Display_1), .clk(clk));  // open: en, clr
  Multiplexer #(.width(16), .enable("false")) multiplexer_11 (
    .in0(Display_1), .in1(rs), .out(multiplexer_11_out), .sel(and_6_out));
  assign or_6_out = and_7_out | bit_extender_4_out;  // OR_Gate or_6, 16 bits wide
  _7_Segment_Display u_7_segment_display_8 (
    .g(blocktop_2_out_11), .f(blocktop_2_out_19), .a(blocktop_2_out_20), .b(blocktop_2_out_12),
    .e(blockbottom_2_out_19), .d(blockbottom_2_out_11), .c(blockbottom_2_out_12), .dp(blockbottom_2_out_20));
  Multiplexer #(.width(16)) multiplexer_12 (.in0(or_6_out), .in1(rs), .out(jump_addr), .sel(jr));  // open: en
  Multiplexer #(.width(16)) multiplexer_13 (
    .in0(Data_Mem_Addr), .in1(imm____8), .out(multiplexer_13_out), .sel(lui));  // open: en
  Multiplexer #(.width(16)) multiplexer_14 (
    .in0(Data_Mem_Data), .in1(multiplexer_13_out), .out(Write_Data), .sel(mem_reg));  // open: en

  // Other names for the same wires on the sheet: target_addr[2:0] = funct; Address_ALU_Result[15:0] = Data_Mem_Addr;
  //   currPC[15:0] = To_Instr_Mem; d0[15:0] = Display_0; d1[15:0] = Display_1; rt[15:0] = Data_In;
  //   sw = Data_Mem_Write

  // Notes on the sheet:
  //   Control
  //   ALU
  //   DISPLAY[0]
  //   Misc Computation
  //   DISPLAY[1]
  //   Memory
endmodule

module opcode (
  input  [3:0] opcode,
  output out_2,
  output out_3,
  output out_4,
  output out_5,
  output out_6,
  output out_7,
  output out_8,
  output out_9,
  output out_10,
  output out_11,
  output out_12,
  output out_13,
  output out_14
);

  wire not_1_out, not_2_out, not_3_out, not_4_out, not_5_out, not_6_out, not_7_out, not_8_out, not_9_out,
       not_10_out, not_11_out, not_12_out, not_13_out, not_14_out, not_15_out, not_16_out, not_17_out,
       not_18_out, not_19_out, not_20_out, not_21_out, not_22_out, not_23_out, not_24_out, not_25_out,
       not_26_out, not_27_out, not_28_out, not_29_out, not_30_out;

  not not_1 (not_1_out, opcode[0]);
  not not_2 (not_2_out, opcode[1]);
  not not_3 (not_3_out, opcode[2]);
  not not_4 (not_4_out, opcode[3]);
  not not_5 (not_5_out, opcode[1]);
  not not_6 (not_6_out, opcode[2]);
  not not_7 (not_7_out, opcode[3]);
  not not_8 (not_8_out, opcode[0]);
  not not_9 (not_9_out, opcode[2]);
  not not_10 (not_10_out, opcode[3]);
  not not_11 (not_11_out, opcode[2]);
  not not_12 (not_12_out, opcode[3]);
  not not_13 (not_13_out, opcode[0]);
  not not_14 (not_14_out, opcode[1]);
  not not_15 (not_15_out, opcode[3]);
  not not_16 (not_16_out, opcode[1]);
  not not_17 (not_17_out, opcode[3]);
  not not_18 (not_18_out, opcode[0]);
  not not_19 (not_19_out, opcode[3]);
  not not_20 (not_20_out, opcode[3]);
  not not_21 (not_21_out, opcode[0]);
  not not_22 (not_22_out, opcode[1]);
  not not_23 (not_23_out, opcode[2]);
  not not_24 (not_24_out, opcode[1]);
  not not_25 (not_25_out, opcode[2]);
  not not_26 (not_26_out, opcode[0]);
  not not_27 (not_27_out, opcode[2]);
  not not_28 (not_28_out, opcode[2]);
  not not_29 (not_29_out, opcode[0]);
  not not_30 (not_30_out, opcode[1]);
  and and_1 (out_2, not_1_out, not_2_out, not_3_out, not_4_out);
  and and_2 (out_3, opcode[0], not_5_out, not_6_out, not_7_out);
  and and_3 (out_4, not_8_out, opcode[1], not_9_out, not_10_out);
  and and_4 (out_5, opcode[0], opcode[1], not_11_out, not_12_out);
  and and_5 (out_6, not_13_out, not_14_out, opcode[2], not_15_out);
  and and_6 (out_7, opcode[0], not_16_out, opcode[2], not_17_out);
  and and_7 (out_8, not_18_out, opcode[1], opcode[2], not_19_out);
  and and_8 (out_9, opcode[0], opcode[1], opcode[2], not_20_out);
  and and_9 (out_10, not_21_out, not_22_out, not_23_out, opcode[3]);
  and and_10 (out_11, opcode[0], not_24_out, not_25_out, opcode[3]);
  and and_11 (out_12, not_26_out, opcode[1], not_27_out, opcode[3]);
  and and_12 (out_13, opcode[0], opcode[1], not_28_out, opcode[3]);
  and and_13 (out_14, not_29_out, not_30_out, opcode[2], opcode[3]);

  // Other names for the same wires on the sheet: opcode_0 = opcode[0]; opcode_1 = opcode[1]; opcode_2 = opcode[2];
  //   opcode_3 = opcode[3]
endmodule
