// Logisim project jaljrlwsw-test.circ as structural Verilog: 1 circuit, main circuit main
module main (
  output [15:0] r0,
  output [15:0] r1,
  output [15:0] r2,
  output [15:0] r3,
  output [15:0] d0,
  output [15:0] d1,
  output [15:0] Clock_Count,
  output [15:0] Data_Mem_Data,
  output [15:0] Data_Mem_Addr,
  output Write_Enabled
);

  wire clock_1_out;
  wire [15:0] adder_1_out, main_1_data_mem_addr, main_1_data_mem_data, main_1_to_instr_mem, rom_1_data;

  ROM #(.addrWidth(16), .dataWidth(16)) rom_1 (.addr(main_1_to_instr_mem), .data(rom_1_data));  // open: sel
  cpu_main main_1 (
    .From_Instr_Mem(rom_1_data), .r0(r0), .r1(r1), .r2(r2), .r3(r3), .Display_0(d0), .Display_1(d1),
    .clk(clock_1_out), .To_Instr_Mem(main_1_to_instr_mem), .Data_Mem_Data(main_1_data_mem_data),
    .Data_Mem_Addr(main_1_data_mem_addr), .Data_Mem_Write(Write_Enabled));  // open: in_2
  Multiplexer #(.width(16), .enable("false")) multiplexer_1 (
    .in0({16{1'b0}}), .in1(main_1_data_mem_data), .out(Data_Mem_Data), .sel(Write_Enabled));
  Multiplexer #(.width(16), .enable("false")) multiplexer_2 (
    .in0({16{1'b0}}), .in1(main_1_data_mem_addr), .out(Data_Mem_Addr), .sel(Write_Enabled));
  Clock clock_1 (.out(clock_1_out));
  Register #(.width(16)) register_1 (.D(adder_1_out), .Q(Clock_Count), .clk(clock_1_out));  // open: en, clr
  Adder #(.width(16)) adder_1 (.a(16'h1), .b(Clock_Count), .out(adder_1_out));  // open: cin, cout

  // Notes on the sheet:
  //   contents of rom_1 (hex, n*v repeats v):
  //   22ff 3aff 4aff ca00 6012 ba00 4a01 600a 2000 7009 600b 600c 459a 183 a83 5f00 3f08 8c00 4aff c800
  //   20ff 3009 b800 4a01 8c00
endmodule
